# Fritzing sketch heater (saved by Fritzing 0.9.4)
circuit board: 5cm x 8cm
breadboards: 1

parts:
  IC1 = IC, DIP package, 6 pins [chip_label=MOC3041]
  IC2 = IC, DIP package, 6 pins [chip_label=MOC3041]
  D1 = Rectifier Diode [part_number=1N4007 package="300 mil [THT]"]
  D2 = Rectifier Diode [part_number=1N4007 package="300 mil [THT]"]
  R1 = Resistor [tolerance=±5% resistance=82 package=THT]
  R2 = Resistor [tolerance=±5% resistance=82 package=THT]
  IC3 = IC, DIP package, 6 pins [chip_label=MOC3041]
  IC4 = IC, DIP package, 6 pins [chip_label=MOC3041]
  D3 = Rectifier Diode [part_number=1N4007 package="300 mil [THT]"]
  R3 = Resistor [tolerance=±5% resistance=82 package=THT]
  R4 = Resistor [tolerance=±5% resistance=82 package=THT]
  IC5 = IC, DIP package, 6 pins [chip_label=MOC3041]
  R5 = Resistor [tolerance=±5% resistance=82 package=THT]
  AC-DC_12V = NCH8200HV
  D4 = Rectifier Diode [part_number=1N4007 package="300 mil [THT]"]
  LM2596 = LM2596 step down module
  J1 = screw terminal, 3 pins
  J2 = screw terminal, 2 pins
  250V = FUSE [package=fuse_5mm]
  XIAO-ESP32-C3 = seeeduino-xiao
  IO = male pin header, 5 pins [form="♂ (male)"]
  D5 = Diode [part_number=1N4148 package=diode-1n4148]

nets:
  N1: IC1.pin1, R1.Pin_1
  GND: IC1.pin2, IC2.pin2, IC3.pin2, IC4.pin2, IC5.pin2, AC-DC_12V.GND, LM2596.IN-, LM2596.OUT-, XIAO-ESP32-C3.GND, IO.pin1
  N2: IC1.pin4, J1.pin3
  N3: IC1.pin6, IC2.pin6, IC3.pin6, IC4.pin6, IC5.pin6, AC-DC_12V.N, 250V.1
  N4: IC2.pin1, R2.Pin_1
  N5: IC2.pin4, D1.cathode
  N6: D1.anode, D2.cathode, J1.pin2
  N7: D2.anode, IC3.pin4
  N8: R1.Pin_0, XIAO-ESP32-C3.D1
  N9: R2.Pin_0, XIAO-ESP32-C3.D2
  N10: IC3.pin1, R3.Pin_1
  N11: IC4.pin1, R4.Pin_1
  N12: IC4.pin4, D3.cathode
  N13: D3.anode, D4.cathode, J1.pin1
  N14: R3.Pin_0, XIAO-ESP32-C3.D3
  N15: R4.Pin_0, XIAO-ESP32-C3.D10
  N16: IC5.pin1, R5.Pin_1
  N17: IC5.pin4, D4.anode
  N18: R5.Pin_0, XIAO-ESP32-C3.D8
  N19: AC-DC_12V.VOUT, LM2596.IN+
  N20: AC-DC_12V.L, J2.pin1
  N21: LM2596.OUT+, D5.A
  N22: J2.pin2, 250V.2
  N23: XIAO-ESP32-C3.D0, IO.pin3
  N24: XIAO-ESP32-C3.D4, IO.pin4
  N25: XIAO-ESP32-C3.D5, IO.pin5
  5V: XIAO-ESP32-C3.5V, IO.pin2, D5.C

notes:
  FP1
  FP2
  EAU
  L
  N
  Danger!
  230V
  SCL
  SDA
  5V
  GND
  D0
  JLCJLCJLCJLC
  2023

custom parts:
  LM2596 step down module: LM2596 DC-DC step down power supply module 3 A.
  seeeduino-xiao: Seeeduino XIAO processor board.
